# Fritzing sketch LegoPWM (saved by Fritzing 1.0.6)
circuit board: 7.6cm x 6.4cm
breadboards: 1

parts:
  ESP32_30-Pin = DOIT Esp32 DevKit v1 (30 pins long, 11 pins width) [part_number=ESP32S-PIN30]
  PCA9685 = male pin header, 6 pins [form="♂ (male)"]

nets:
  N1: ESP32_30-Pin.3V3, PCA9685.pin2
  N2: ESP32_30-Pin.GND, PCA9685.pin6
  N3: ESP32_30-Pin.D32, PCA9685.pin3
  N4: ESP32_30-Pin.D33, PCA9685.pin4
  N5: ESP32_30-Pin.VIN, PCA9685.pin1

notes:
  GND
  PCA9685
  BrickLight Ver.: 1.0
  Marcel Hauri - 2026
  OE
  SCL
  SDA
  VCC
  V+

custom parts:
  DOIT Esp32 DevKit v1 (30 pins long, 11 pins width): The DOIT Esp32 DevKit v1 is one of the development board created by DOIT to evaluate the ESP-WROOM-32 module. It is based on the ESP32 microcontroller that boasts Wifi, Bluetooth, Ethernet and Low Power support all in a single chip. (vanepp) made breadboard work, adjusted pin numbering and labels and reduced size of schematic and cleaned up pcb. This chip is 30pins long (2 x15) and 11 pins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
